// Logisim project code_lock.circ as structural Verilog: 9 circuits, main circuit main
module main (
  input  a,
  input  b,
  input  c,
  input  reset,
  output LED
);

  wire button_decoder_1_error, button_decoder_1_x0, button_decoder_1_x1, clk_out, edge_detect_1_btn_out,
       edge_detect_2_btn_out, edge_detect_3_btn_out;
  wire [2:0] fsm_1_q0;

  Clock clk (.out(clk_out));
  edge_detect edge_detect_1 (.reset(reset), .btn_in(a), .clk(clk_out), .btn_out(edge_detect_1_btn_out));
  edge_detect edge_detect_2 (.reset(reset), .btn_in(b), .clk(clk_out), .btn_out(edge_detect_2_btn_out));
  edge_detect edge_detect_3 (.reset(reset), .btn_in(c), .clk(clk_out), .btn_out(edge_detect_3_btn_out));
  button_decoder button_decoder_1 (
    .a(edge_detect_1_btn_out), .b(edge_detect_2_btn_out), .c(edge_detect_3_btn_out), .reset(reset),
    .x1(button_decoder_1_x1), .x0(button_decoder_1_x0), .error(button_decoder_1_error));
  Hex_Digit_Display #(.decimalPoint("false")) hex_digit_display_1 (.value({1'b0, fsm_1_q0}));
  fsm fsm_1 (
    .x1(button_decoder_1_x1), .x0(button_decoder_1_x0), .CLK(clk_out), .RESET(button_decoder_1_error),
    .q2(fsm_1_q0[2]), .q1(fsm_1_q0[1]), .q0(fsm_1_q0[0]), .LED(LED));
endmodule

module button_decoder (
  input  a,
  input  b,
  input  c,
  input  reset,
  output x1,
  output x0,
  output error
);

  wire and_1_out, and_2_out, and_3_out, and_4_out;

  or or_1 (x1, b, c);
  or or_2 (x0, a, c);
  and and_1 (and_1_out, a, b);
  and and_2 (and_2_out, a, c);
  and and_3 (and_3_out, b, c);
  and and_4 (and_4_out, a, b, c);
  or or_3 (error, and_1_out, and_2_out, and_3_out, reset, and_4_out);
endmodule

module fsm (
  input  x1,
  input  x0,
  input  CLK,
  input  RESET,
  output q2,
  output q1,
  output q0,
  output LED
);

  wire d0_func_1_d0, d1_func_1_d1, d2_func_1_d2, input_encoding_1_a, input_encoding_1_b, input_encoding_1_c,
       input_encoding_1_n, state_encoding_1_s0, state_encoding_1_s1, state_encoding_1_s2, state_encoding_1_s3;

  input_encoding input_encoding_1 (
    .x1(x1), .x0(x0), .n(input_encoding_1_n), .a(input_encoding_1_a), .b(input_encoding_1_b),
    .c(input_encoding_1_c));
  d2_func d2_func_1 (
    .s3(state_encoding_1_s3), .s4(LED), .c(input_encoding_1_c), .n(input_encoding_1_n), .d2(d2_func_1_d2));
  d1_func d1_func_1 (
    .s1(state_encoding_1_s1), .s2(state_encoding_1_s2), .s3(state_encoding_1_s3), .c(input_encoding_1_c),
    .n(input_encoding_1_n), .b(input_encoding_1_b), .d1(d1_func_1_d1));
  d0_func d0_func_1 (
    .s0(state_encoding_1_s0), .s1(state_encoding_1_s1), .s2(state_encoding_1_s2), .s3(state_encoding_1_s3),
    .a(input_encoding_1_a), .n(input_encoding_1_n), .b(input_encoding_1_b), .d0(d0_func_1_d0));
  D_Flip_Flop d_ff_1 (.D(d2_func_1_d2), .clk(CLK), .Q(q2), .reset(RESET));  // open: Qn, preset
  D_Flip_Flop d_ff_2 (.D(d1_func_1_d1), .clk(CLK), .Q(q1), .reset(RESET));  // open: Qn, preset
  D_Flip_Flop d_ff_3 (.D(d0_func_1_d0), .clk(CLK), .Q(q0), .reset(RESET));  // open: Qn, preset
  state_encoding state_encoding_1 (
    .q2(q2), .q1(q1), .q0(q0), .s0(state_encoding_1_s0), .s1(state_encoding_1_s1), .s2(state_encoding_1_s2),
    .s3(state_encoding_1_s3), .s4(LED));
endmodule

module d0_func (
  input  s0,
  input  s1,
  input  s2,
  input  s3,
  input  a,
  input  n,
  input  b,
  output d0
);

  wire and_1_out, and_2_out, and_3_out, and_4_out;

  and and_1 (and_1_out, s0, a);
  and and_2 (and_2_out, s1, n);
  and and_3 (and_3_out, s2, b);
  and and_4 (and_4_out, s3, n);
  or or_1 (d0, and_1_out, and_2_out, and_3_out, and_4_out);
endmodule

module d1_func (
  input  s1,
  input  s2,
  input  s3,
  input  c,
  input  n,
  input  b,
  output d1
);

  wire and_1_out, and_2_out, and_3_out, and_4_out;

  and and_1 (and_1_out, s1, c);
  and and_2 (and_2_out, s2, n);
  and and_3 (and_3_out, s2, b);
  and and_4 (and_4_out, s3, n);
  or or_1 (d1, and_1_out, and_2_out, and_3_out, and_4_out);
endmodule

module d2_func (
  input  s3,
  input  s4,
  input  c,
  input  n,
  output d2
);

  wire and_1_out, and_2_out;

  and and_1 (and_1_out, s3, c);
  and and_2 (and_2_out, s4, n);
  or or_1 (d2, and_1_out, and_2_out);
endmodule

module edge_detect (
  input  reset,
  input  btn_in,
  input  clk,
  output btn_out
);

  wire d_ff_1_q, debounce_logisim_1_p4, not_1_out;

  // debounce_logisim debounce_logisim_1: pin names not known; wires that end beside it: reset, clk, btn_in, debounce_logisim_1_p4
  D_Flip_Flop d_ff_1 (.D(debounce_logisim_1_p4), .clk(clk), .Q(d_ff_1_q), .reset(reset));  // open: Qn, preset
  not not_1 (not_1_out, d_ff_1_q);
  and and_1 (btn_out, debounce_logisim_1_p4, not_1_out);
endmodule

module state_encoding (
  input  q2,
  input  q1,
  input  q0,
  output s0,
  output s1,
  output s2,
  output s3,
  output s4
);

  wire not_1_out, not_2_out, not_3_out;

  not not_1 (not_1_out, q2);
  not not_2 (not_2_out, q1);
  not not_3 (not_3_out, q0);
  and and_1 (s0, not_1_out, not_2_out, not_3_out);
  and and_2 (s1, not_1_out, not_2_out, q0);
  and and_3 (s2, not_1_out, q1, not_3_out);
  and and_4 (s3, not_1_out, q1, q0);
  and and_5 (s4, q2, not_2_out, not_3_out);
endmodule

module input_encoding (
  input  x1,
  input  x0,
  output n,
  output a,
  output b,
  output c
);

  wire not_1_out, not_2_out;

  not not_1 (not_1_out, x1);
  not not_2 (not_2_out, x0);
  and and_1 (n, not_1_out, not_2_out);
  and and_2 (a, not_1_out, x0);
  and and_3 (b, x1, not_2_out);
  and and_4 (c, x1, x0);
endmodule
